# Fritzing sketch BrainyHead (saved by Fritzing 1.0.5)
# 18650 Li-ion Battery: CC-BY Dr Kristofer Chan, King's College London/Remote-research.org
breadboards: 1

parts:
  ESP32_-_Front1 = ESP32 - CAM
  Part1 = ESP3 NODE32S
  Part2 = Adafruit MAX9814 Electret Microphone Amplifier [part_number="Adafruit #1713"]
  M1 = PAM8403 Stereo Amplifier [part_number=HW-104]
  SP1 = SPEAKER [package=pcb_mount_speaker]
  SP2 = SPEAKER [package=pcb_mount_speaker]
  OLED_I2C1 = OLED 128x64 I2C Monochrome Display
  J1 = Basic Servo
  J2 = Basic Servo
  J3 = Basic Servo
  U1 = LM2596 step down module
  Part3 = Thumb Joystick
  S1 = SWITCH-SPST-2 [package=switch-spst-vertical]
  BAT1 = 18650 Li-ion Battery [package=battery-18650]
  BAT2 = 18650 Li-ion Battery [package=battery-18650]

nets:
  N1: ESP32_-_Front1.GPIO4, Part2.OUTPUT
  GND: ESP32_-_Front1.GND, Part1.GND, Part2.GND, Part2.GAIN, M1.POWER-, M1.INPUTG, OLED_I2C1.GND, J1.gnd, J2.gnd, J3.gnd, U1.IN-, U1.OUT-, Part3.GND, BAT2.-
  VCC: ESP32_-_Front1.5V, Part1.5V, M1.POWER+, OLED_I2C1.VDD, J2.vcc, J3.vcc, U1.OUT+, Part3.VCC
  3.3V: ESP32_-_Front1.3.3V, Part2.VDD
  N2: ESP32_-_Front1.GPIO3_/_RX, Part1.IO17
  N3: ESP32_-_Front1.GPIO1_/_TX, Part1.IO16
  N4: Part1.IO34, Part3.VERT
  N5: Part1.IO35, Part3.HORZ
  N6: Part1.IO32, Part3.SEL
  N7: Part1.IO25, M1.INPUTL
  N8: Part1.IO26, M1.INPUTR
  N9: Part1.IO23, J3.pulse
  N10: Part1.IO22, OLED_I2C1.SCK
  N11: Part1.IO21, OLED_I2C1.SDA
  N12: Part1.IO19, J2.pulse
  N13: Part1.IO18, J1.pulse
  N14: M1.ROUT-, SP2.+
  N15: M1.ROUT+, SP2.-
  N16: M1.LOUT+, SP1.-
  N17: M1.LOUT-, SP1.+
  N18: U1.IN+, S1.O
  N19: S1.P, BAT1.+
  N20: BAT1.-, BAT2.+

notes:
  neck_XY
  neck_XZ
  neck_YZ
  5V Regulator

custom parts:
  ESP32 - CAM: The ESP32-CAM has a very competitive small-size camera module that can operate independently as a minimum system with a footprint of only 27*40.5*4.5mm and a deep sleep current of up to 6mA.
  Adafruit MAX9814 Electret Microphone Amplifier: Add an ear to your project with this well-designed electret microphone amplifier with AGC. This fully assembled and tested board comes with a 20-20KHz electret microphone soldered on. For the amplification, we use the Maxim MAX9814, a specialty chip that is designed for amplifying electret microphones in situations where the loudness of the audio isn't predictable. This fancy microphone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
  PAM8403 Stereo Amplifier: PAM8403 stereo amplifier module Descriptive words Links: PAM8403 product datasheet
  LM2596 step down module: LM2596 DC-DC step down power supply module 3 A.
  18650 Li-ion Battery: 18650 li-ion Battery Standard 18650 battery with interactive connectors Creative Common Attribution 4.0 International (CC-BY 4.0) license. Any use of this part requires attribution of Dr Kristofer Chan, Department of Geography, King's College London. Contact kristofer.chan [at] kcl.ac.uk OR kris [at] remote-research.org for further information.
